# Fritzing sketch Santa Trap (saved by Fritzing 1.0.3b)
breadboards: 1

parts:
  Mod1 = Raspberry Pi Pico
  LED1 = LED - 5mm [color="Red (633nm)" current=0.030A package="5 mm [THT]"]
  R1 = Resistor [tolerance=±5% power=0.25W resistance=220 package=THT]
  PIR1 = PIR sensor
  J1 = Piezo Speaker

nets:
  N1: Mod1.pin_3, Mod1.pin_8, Mod1.pin_13, Mod1.pin_18, Mod1.pin_23, Mod1.pin_28, Mod1.pin_33, Mod1.pin_38, Mod1.pin_42, R1.Pin_0, PIR1.GND, J1.pin1
  N2: Mod1.pin_20, PIR1.SIG
  N3: Mod1.pin_21, LED1.anode
  N4: Mod1.pin_22, J1.pin2
  N5: Mod1.pin_40, PIR1.VDD
  N6: LED1.cathode, R1.Pin_1

custom parts:
  Raspberry Pi Pico: Raspberry Pi Pico. Based around the RP2040 microcontroller the Pico is a low cost microcontroller device bringing Raspberry Pi quality, cost, and easy of use to the microcontroller space. Jan 2021, Split part in to two versions: tht (this one) and SMD. This one will drill holes for a .1 in header in pcb to allow plugging in the module as well as providing pads to solder the module to the top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
